// Logisim project KeySelector.circ as structural Verilog: 1 circuit, main circuit main
module main (
);

  wire and_1_out, and_2_out, and_3_out, and_4_out, and_5_out, and_6_out, and_7_out, and_8_out, and_9_out,
       and_10_out, and_11_out, and_12_out, and_13_out, button_1_out, button_2_out, clock_1_out, clock_2_out,
       clock_3_out, LE_out, MAN_INPUT_out, multiplexer_1_out, multiplexer_2_out, nor_1_out, nor_2_out,
       nor_3_out, nor_4_out, not_1_out, or_1_out, or_2_out, or_3_out, or_4_out, or_5_out, or_6_out, or_7_out,
       or_8_out, or_9_out, SHIFT_out, shift_register_1_p5, shift_register_1_p6, shift_register_1_p7,
       shift_register_1_p8, shift_register_1_p9, shift_register_1_p10, shift_register_1_p11,
       shift_register_1_p12, shift_register_1_p13, shift_register_1_p14, shift_register_1_p15,
       shift_register_1_p16, undriven, undriven_2, undriven_3, undriven_4, xor_1_out, xor_2_out, xor_3_out;
  wire [1:0] j_k_ff_1_q;
  wire [3:0] d_q, j_k_ff_3_q, register_1_q;

  J_K_Flip_Flop d (.J(1'b1), .K(1'b1), .clk(clock_1_out), .Q(d_q[0]));  // open: Qn, preset, reset
  Clock clock_1 (.out(clock_1_out));
  J_K_Flip_Flop j_k_ff_1 (.J(1'b1), .K(1'b1), .clk(button_1_out), .Q(j_k_ff_1_q[0]));  // open: Qn, preset, reset
  Button button_1 (.out(button_1_out));
  J_K_Flip_Flop c (.J(d_q[0]), .K(d_q[0]), .clk(clock_1_out), .Q(d_q[1]));  // open: Qn, preset, reset
  xor xor_1 (xor_1_out, d_q[3], d_q[2]);
  nor nor_1 (nor_1_out, d_q[1], d_q[0]);
  xor xor_2 (xor_2_out, d_q[2], d_q[0]);
  not not_1 (not_1_out, d_q[0]);
  and and_1 (and_1_out, not_1_out, d_q[2]);
  and and_2 (and_2_out, d_q[1], d_q[0]);
  J_K_Flip_Flop j_k_ff_2 (
    .J(j_k_ff_1_q[0]), .K(j_k_ff_1_q[0]), .clk(button_1_out), .Q(j_k_ff_1_q[1]));  // open: Qn, preset, reset
  and and_3 (and_3_out, d_q[0], d_q[1]);
  and and_4 (and_4_out, and_3_out, d_q[2]);
  J_K_Flip_Flop b (.J(and_3_out), .K(and_3_out), .clk(clock_1_out), .Q(d_q[2]));  // open: Qn, preset, reset
  and and_5 (and_5_out, d_q[2], nor_1_out);
  and and_6 (and_6_out, xor_1_out, d_q[0]);
  or or_1 (or_1_out, and_6_out, nor_2_out);
  nor nor_2 (nor_2_out, xor_1_out, d_q[0]);
  nor nor_3 (nor_3_out, d_q[3], xor_2_out);
  and and_7 (and_7_out, d_q[3], d_q[1]);
  or or_2 (or_2_out, nor_1_out, and_1_out);
  or or_3 (or_3_out, nor_3_out, and_2_out);
  J_K_Flip_Flop a (.J(and_4_out), .K(and_4_out), .clk(clock_1_out), .Q(d_q[3]));  // open: Qn, preset, reset
  Button #(.press("passive")) MAN_INPUT (.out(MAN_INPUT_out));
  or or_4 (or_4_out, and_5_out, or_1_out);
  or or_5 (or_5_out, nor_3_out, and_8_out);
  and and_8 (and_8_out, and_7_out, xor_2_out);
  and and_9 (and_9_out, or_2_out, d_q[3]);
  or or_6 (or_6_out, and_9_out, or_3_out);
  xor xor_3 (xor_3_out, j_k_ff_1_q[0], j_k_ff_1_q[1]);
  Button SHIFT (.out(SHIFT_out));
  Button LE (.out(LE_out));
  Clock clock_2 (.out(clock_2_out));
  or or_7 (or_7_out, nor_1_out, or_5_out);
  nor nor_4 (nor_4_out, LE_out, SHIFT_out);
  or or_8 (or_8_out, nor_4_out, xor_3_out);
  and and_10 (and_10_out, LE_out, clock_2_out);
  or or_9 (or_9_out, nor_4_out, and_10_out);
  Multiplexer #(.select(2)) multiplexer_1 (
    .in0(or_4_out), .in1(or_6_out), .in2(or_7_out), .in3(MAN_INPUT_out), .out(multiplexer_1_out),
    .sel(j_k_ff_1_q));  // open: en
  J_K_Flip_Flop j_k_ff_3 (.J(1'b1), .K(1'b1), .clk(button_2_out), .Q(j_k_ff_3_q[0]));  // open: Qn, preset, reset
  Button button_2 (.out(button_2_out));
  // Shift_Register #(.length(16)) shift_register_1: pin names not known; wires that end beside it: or_8_out, 1'b1, or_9_out, multiplexer_1_out, shift_register_1_p5, shift_register_1_p6, shift_register_1_p7, shift_register_1_p8, shift_register_1_p9, shift_register_1_p10, shift_register_1_p11, shift_register_1_p12, shift_register_1_p13, shift_register_1_p14, shift_register_1_p15, shift_register_1_p16
  J_K_Flip_Flop j_k_ff_4 (
    .J(j_k_ff_3_q[0]), .K(j_k_ff_3_q[0]), .clk(button_2_out), .Q(j_k_ff_3_q[1]));  // open: Qn, preset, reset
  and and_11 (and_11_out, j_k_ff_3_q[0], j_k_ff_3_q[1]);
  J_K_Flip_Flop j_k_ff_5 (
    .J(and_11_out), .K(and_11_out), .clk(button_2_out), .Q(j_k_ff_3_q[2]));  // open: Qn, preset, reset
  and and_12 (and_12_out, and_11_out, j_k_ff_3_q[2]);
  J_K_Flip_Flop j_k_ff_6 (
    .J(and_12_out), .K(and_12_out), .clk(button_2_out), .Q(j_k_ff_3_q[3]));  // open: Qn, preset, reset
  Clock clock_3 (.out(clock_3_out));
  and and_13 (and_13_out, clock_3_out, multiplexer_2_out);
  Multiplexer #(.select(4)) multiplexer_2 (
    .in0(shift_register_1_p6), .in1(shift_register_1_p7), .in2(shift_register_1_p8),
    .in3(shift_register_1_p9), .in4(shift_register_1_p10), .in5(shift_register_1_p11),
    .in6(shift_register_1_p12), .in7(shift_register_1_p13), .in8(shift_register_1_p14),
    .in9(shift_register_1_p15), .in10(shift_register_1_p16), .in11(undriven), .in12(undriven_2),
    .in13(undriven_3), .in14(undriven_4), .in15(shift_register_1_p5), .out(multiplexer_2_out),
    .sel(j_k_ff_3_q), .en(1'b1));
  Register #(.width(4)) register_1 (.D(j_k_ff_3_q), .en(1'b1), .clk(and_13_out), .Q(register_1_q));  // open: clr
  Hex_Digit_Display hex_digit_display_1 (.value(j_k_ff_3_q));  // open: dp
  Hex_Digit_Display hex_digit_display_2 (.value(register_1_q));  // open: dp
endmodule
