// Logisim project Prescaler_PRIO_ENC.circ as structural Verilog: 1 circuit, main circuit main
module main (
);

  wire button_1_out, button_2_out, button_3_out, button_4_out, button_5_out, button_6_out, button_7_out,
       button_8_out, button_9_out, button_10_out, button_11_out, button_12_out, button_13_out, button_14_out,
       button_15_out, button_16_out, not_1_out, or_1_out, or_2_out, or_3_out, or_4_out,
       priority_encoder_1_en_out, priority_encoder_1_gs, priority_encoder_2_gs;
  wire [2:0] priority_encoder_1_out, priority_encoder_2_out;

  Button button_1 (.out(button_1_out));
  Button button_2 (.out(button_2_out));
  Button button_3 (.out(button_3_out));
  Button button_4 (.out(button_4_out));
  Button button_5 (.out(button_5_out));
  Button button_6 (.out(button_6_out));
  Button button_7 (.out(button_7_out));
  Button button_8 (.out(button_8_out));
  Button button_9 (.out(button_9_out));
  Button button_10 (.out(button_10_out));
  Button button_11 (.out(button_11_out));
  Button button_12 (.out(button_12_out));
  Button button_13 (.out(button_13_out));
  Button button_14 (.out(button_14_out));
  Button button_15 (.out(button_15_out));
  Button button_16 (.out(button_16_out));
  Priority_Encoder priority_encoder_1 (
    .in0(button_1_out), .in1(button_2_out), .in2(button_3_out), .in3(button_4_out), .in4(button_5_out),
    .in5(button_6_out), .in6(button_7_out), .in7(button_8_out), .out(priority_encoder_1_out), .en_in(1'b1),
    .gs(priority_encoder_1_gs), .en_out(priority_encoder_1_en_out));
  Priority_Encoder priority_encoder_2 (
    .in0(button_9_out), .in1(button_10_out), .in2(button_11_out), .in3(button_12_out), .in4(button_13_out),
    .in5(button_14_out), .in6(button_15_out), .in7(button_16_out), .out(priority_encoder_2_out),
    .en_in(priority_encoder_1_en_out), .gs(priority_encoder_2_gs));  // open: en_out
  not not_1 (not_1_out, priority_encoder_1_en_out);
  or or_1 (or_1_out, priority_encoder_1_out[0], priority_encoder_2_out[0]);
  or or_2 (or_2_out, priority_encoder_1_out[1], priority_encoder_2_out[1]);
  or or_3 (or_3_out, priority_encoder_1_out[2], priority_encoder_2_out[2]);
  or or_4 (or_4_out, priority_encoder_1_gs, priority_encoder_2_gs);
  LED led_1 (.in(or_1_out));
  LED led_2 (.in(or_2_out));
  LED led_3 (.in(or_3_out));
  LED led_4 (.in(not_1_out));
  LED led_5 (.in(or_4_out));
endmodule
